// Logisim project 1termin3zad.circ as structural Verilog: 3 circuits, main circuit main
module main (
  input  SYNC,
  input  [3:0] \input ,
  output ACK,
  output [3:0] \output ,
  output WYN
);

  wire clock_1_out, multiplexer_1_out, not_1_out, not_2_out;
  wire [1:0] rom_1_data_3;
  wire [2:0] counter_1_q, rom_1_data;
  wire [3:0] A_q, B_q, sumZM_y, ZMtoU2_y;
  wire [8:3] rom_1_data_2;

  Clock clock_1 (.out(clock_1_out));
  Register #(.width(4)) A (.D(\input ), .en(rom_1_data_2[3]), .Q(A_q), .clk(clock_1_out));  // open: clr
  sumZM sumZM (.A(A_q), .B(B_q), .Y(sumZM_y));
  ZMtoU2 ZMtoU2 (.X(sumZM_y), .Y(ZMtoU2_y));
  Register #(.width(4)) B (.D(\input ), .en(rom_1_data_2[4]), .Q(B_q), .clk(clock_1_out));  // open: clr
  Register #(.width(4)) Y (.D(ZMtoU2_y), .en(rom_1_data_2[5]), .Q(\output ), .clk(clock_1_out), .clr(rom_1_data_2[6]));
  not not_1 (not_1_out, SYNC);
  D_Flip_Flop d_ff_1 (
    .clk(1'b0), .D(1'b0), .Q(ACK), .preset(rom_1_data_2[7]), .reset(rom_1_data_2[8]));  // open: Qn, en
  Multiplexer #(.select(2), .enable("false")) multiplexer_1 (
    .in0(SYNC), .in1(not_1_out), .in2(1'b0), .in3(1'b0), .out(multiplexer_1_out), .sel(rom_1_data_3));
  not not_2 (not_2_out, multiplexer_1_out);
  Counter #(.width(3), .max('h6), .trigger("falling")) counter_1 (
    .load(not_2_out), .D(rom_1_data), .count(multiplexer_1_out), .Q(counter_1_q), .clk(clock_1_out));  // open: carry, clr
  ROM #(.addrWidth(3), .dataWidth(12)) rom_1 (
    .addr(counter_1_q), .data({rom_1_data_3, WYN, rom_1_data_2, rom_1_data}));  // open: sel

  // Notes on the sheet:
  //   contents of rom_1 (hex, n*v repeats v):
  //   148 481 102 814 825 685 800
endmodule

module sumZM (
  input  [3:0] A,
  input  [3:0] B,
  output [3:0] Y
);

  wire comparator_1_gt, not_1_out, xnor_1_out;
  wire [2:0] adder_1_out, multiplexer_1_out, multiplexer_2_out, subtractor_1_out;

  Comparator #(.width(3), .mode("unsigned")) comparator_1 (
    .a(A[2:0]), .b(B[2:0]), .gt(comparator_1_gt));  // open: eq, lt
  not not_1 (not_1_out, comparator_1_gt);
  Multiplexer #(.width(3), .enable("false")) multiplexer_1 (
    .in0(A[2:0]), .in1(B[2:0]), .out(multiplexer_1_out), .sel(not_1_out));
  Multiplexer #(.width(3), .enable("false")) multiplexer_2 (
    .in0(B[2:0]), .in1(A[2:0]), .out(multiplexer_2_out), .sel(not_1_out));
  Multiplexer #(.enable("false")) multiplexer_3 (.in0(A[3]), .in1(B[3]), .out(Y[3]), .sel(not_1_out));
  xnor xnor_1 (xnor_1_out, A[3], B[3]);
  Subtractor #(.width(3)) subtractor_1 (
    .a(multiplexer_2_out), .b(multiplexer_1_out), .out(subtractor_1_out));  // open: bin, bout
  Multiplexer #(.width(3), .enable("false")) multiplexer_4 (
    .in0(subtractor_1_out), .in1(adder_1_out), .out(Y[2:0]), .sel(xnor_1_out));
  Adder #(.width(3)) adder_1 (.a(B[2:0]), .b(A[2:0]), .out(adder_1_out));  // open: cin, cout
endmodule

module ZMtoU2 (
  input  [3:0] X,
  output [3:0] Y
);

  wire not_1_out;
  wire [2:0] adder_1_out, not_2_out;

  not not_1 (not_1_out, X[3]);
  assign not_2_out = ~X[2:0];  // NOT_Gate not_2, 3 bits wide
  Multiplexer #(.width(4), .enable("false")) multiplexer_1 (
    .in0({X[3], adder_1_out}), .in1(X), .out(Y), .sel(not_1_out));
  Adder #(.width(3)) adder_1 (.a(3'b001), .b(not_2_out), .out(adder_1_out));  // open: cin, cout
endmodule
