// Logisim project uklady.circ as structural Verilog: 2 circuits, main circuit zad1
module zad1 (
  input  x4,
  input  x3,
  input  x2,
  input  x1,
  input  x0,
  output y
);

  wire nand_1_out, nand_2_out, nand_3_out, nand_4_out, nand_5_out, not_1_out, not_2_out, not_3_out,
       not_4_out, not_5_out;

  not not_1 (not_1_out, x3);
  not not_2 (not_2_out, x4);
  not not_3 (not_3_out, x2);
  not not_4 (not_4_out, x1);
  not not_5 (not_5_out, x0);
  nand nand_1 (nand_1_out, not_2_out, not_1_out, not_5_out);
  nand nand_2 (nand_2_out, not_2_out, x2, not_4_out);
  nand nand_3 (nand_3_out, x3, not_3_out, x1, x0);
  nand nand_4 (nand_4_out, x3, x2, not_4_out, not_5_out);
  nand nand_5 (nand_5_out, not_2_out, not_1_out, x1);
  nand nand_6 (y, nand_1_out, nand_2_out, nand_3_out, nand_4_out, nand_5_out);

  // Notes on the sheet:
  //   Bartłomiej Rasztabiga
endmodule

module zad2 (
  input  x4,
  input  x3,
  input  x2,
  input  x1,
  input  x0,
  output y
);

  wire nor_1_out, nor_2_out, nor_3_out, nor_4_out, nor_5_out, not_1_out, not_2_out, not_3_out, not_4_out,
       not_5_out;

  not not_1 (not_1_out, x3);
  not not_2 (not_2_out, x4);
  not not_3 (not_3_out, x2);
  not not_4 (not_4_out, x1);
  not not_5 (not_5_out, x0);
  nor nor_1 (nor_1_out, x2, x1, not_5_out);
  nor nor_2 (nor_2_out, not_1_out, not_3_out, not_4_out);
  nor nor_3 (nor_3_out, not_2_out, x3);
  nor nor_4 (nor_4_out, not_1_out, x2, x0);
  nor nor_5 (nor_5_out, not_2_out, not_3_out, not_5_out);
  nor nor_6 (y, nor_1_out, nor_2_out, nor_3_out, nor_4_out, nor_5_out);

  // Notes on the sheet:
  //   Bartłomiej Rasztabiga
endmodule
