// Logisim project zad1.circ as structural Verilog: 2 circuits, main circuit main
module main (
  input  a7,
  input  b7,
  input  a6,
  input  b6,
  input  a5,
  input  b5,
  input  a4,
  input  b4,
  input  a3,
  input  b3,
  input  a2,
  input  b2,
  input  a1,
  input  b1,
  input  a0,
  input  b0,
  output p1,
  output p0
);

  wire blok_1_p0__i_1, blok_1_p1__i_1, blok_2_p0__i_1, blok_2_p1__i_1, blok_3_p0__i_1, blok_3_p1__i_1,
       blok_4_p0__i_1, blok_4_p1__i_1, blok_5_p0__i_1, blok_5_p1__i_1, blok_6_p0__i_1, blok_6_p1__i_1,
       blok_7_p0__i_1, blok_7_p1__i_1;

  blok blok_1 (.a__i(a7), .b__i(b7), .p1__i(1'b0), .p0__i(1'b0), .p1__i_1(blok_1_p1__i_1), .p0__i_1(blok_1_p0__i_1));
  blok blok_2 (
    .a__i(a6), .b__i(b6), .p1__i(blok_1_p1__i_1), .p0__i(blok_1_p0__i_1), .p1__i_1(blok_2_p1__i_1),
    .p0__i_1(blok_2_p0__i_1));
  blok blok_3 (
    .a__i(a5), .b__i(b5), .p1__i(blok_2_p1__i_1), .p0__i(blok_2_p0__i_1), .p1__i_1(blok_3_p1__i_1),
    .p0__i_1(blok_3_p0__i_1));
  blok blok_4 (
    .a__i(a4), .b__i(b4), .p1__i(blok_3_p1__i_1), .p0__i(blok_3_p0__i_1), .p1__i_1(blok_4_p1__i_1),
    .p0__i_1(blok_4_p0__i_1));
  blok blok_5 (
    .a__i(a3), .b__i(b3), .p1__i(blok_4_p1__i_1), .p0__i(blok_4_p0__i_1), .p1__i_1(blok_5_p1__i_1),
    .p0__i_1(blok_5_p0__i_1));
  blok blok_6 (
    .a__i(a2), .b__i(b2), .p1__i(blok_5_p1__i_1), .p0__i(blok_5_p0__i_1), .p1__i_1(blok_6_p1__i_1),
    .p0__i_1(blok_6_p0__i_1));
  blok blok_7 (
    .a__i(a1), .b__i(b1), .p1__i(blok_6_p1__i_1), .p0__i(blok_6_p0__i_1), .p1__i_1(blok_7_p1__i_1),
    .p0__i_1(blok_7_p0__i_1));
  blok blok_8 (.a__i(a0), .b__i(b0), .p1__i(blok_7_p1__i_1), .p0__i(blok_7_p0__i_1), .p1__i_1(p1), .p0__i_1(p0));
endmodule

module blok (
  input  a__i,
  input  b__i,
  input  p1__i,
  input  p0__i,
  output p1__i_1,
  output p0__i_1
);

  wire and_1_out, and_2_out, not_1_out, not_2_out, not_3_out, not_4_out;

  not not_1 (not_1_out, a__i);
  not not_2 (not_2_out, b__i);
  not not_3 (not_3_out, p1__i);
  not not_4 (not_4_out, p0__i);
  and and_1 (and_1_out, not_1_out, b__i, not_4_out);
  or or_1 (p1__i_1, and_1_out, p1__i);
  and and_2 (and_2_out, a__i, not_2_out, not_3_out);
  or or_2 (p0__i_1, and_2_out, p0__i);
endmodule
