// Logisim project zad2.circ as structural Verilog: 1 circuit, main circuit main
module main (
  input  x3,
  input  x2,
  input  x1,
  input  x0,
  output y1,
  output y2,
  output y3
);

  wire not_1_out, not_2_out, not_3_out, x2_prime_x1_prime_out, x2x1_out, x3_prime_x1_prime_out,
       x3_prime_x2_prime_out, x3x1_out, x3x2x1_out;

  not not_1 (not_1_out, x3);
  not not_2 (not_2_out, x2);
  not not_3 (not_3_out, x1);
  nand x3x2x1 (x3x2x1_out, x3, x2, x1);
  nand x3_prime_x2_prime (x3_prime_x2_prime_out, not_1_out, not_2_out);
  nand x2_prime_x1_prime (x2_prime_x1_prime_out, not_2_out, not_3_out);
  nand x2x1 (x2x1_out, x2, x1);
  nand x3_prime_x1_prime (x3_prime_x1_prime_out, not_1_out, not_3_out);
  nand x3x1 (x3x1_out, x3, x1);
  nand nand_1 (y1, x3x2x1_out, x3_prime_x2_prime_out);
  nand nand_2 (y2, x2_prime_x1_prime_out, x2x1_out);
  nand nand_3 (y3, x2x1_out, x3_prime_x1_prime_out, x3x1_out);
endmodule
