// Logisim project zad1.circ as structural Verilog: 3 circuits, main circuit main
module main (
  input  X1,
  input  X0,
  output y1,
  output y0
);

  wire clock_1_out, l0_1_l1_prime, l1_1_l1_prime;

  L1 l1_1 (.L1(y1), .L0(y0), .X1(X1), .X0(X0), .L1_prime(l1_1_l1_prime));
  L0 l0_1 (.L1_prime(l0_1_l1_prime), .L1(y1), .L0(y0), .X1(X1), .X0(X0));
  Clock clock_1 (.out(clock_1_out));
  D_Flip_Flop L1_2 (.clk(clock_1_out), .D(l1_1_l1_prime), .Q(y1));  // open: Qn, preset, en, reset
  D_Flip_Flop L0_2 (.clk(clock_1_out), .D(l0_1_l1_prime), .Q(y0));  // open: Qn, preset, en, reset

  // Notes on the sheet:
  //   Bartłomiej Rasztabiga
endmodule

// L1'
module L1 (
  input  L1,
  input  L0,
  input  X1,
  input  X0,
  output L1_prime
);

  wire not_1_out;

  not not_1 (not_1_out, L1);
  Multiplexer #(.select(2)) multiplexer_1 (
    .in0(1'b1), .in1(not_1_out), .in2(not_1_out), .in3(not_1_out), .out(L1_prime), .sel({X1, X0}));  // open: en
endmodule

// L0'
module L0 (
  input  L1,
  input  L0,
  input  X1,
  input  X0,
  output L1_prime
);

  wire not_1_out;

  not not_1 (not_1_out, X0);
  Multiplexer #(.select(3)) multiplexer_1 (
    .in0(1'b0), .in1(1'b1), .in2(X0), .in3(1'b0), .in4(X0), .in5(X0), .in6(1'b0), .in7(not_1_out),
    .out(L1_prime), .sel({L1, L0, X1}));  // open: en
endmodule
