// Logisim project zad2.circ as structural Verilog: 4 circuits, main circuit main
module main (
  input  x1,
  input  x0,
  output y
);

  wire clock_1_out, nand_1_out, not_1_out, not_2_out, q0_1_q0_prime_j, q0_1_q0_prime_k, Q0_2_q,
       q1_1_q1_prime_j, q1_1_q1_prime_k, Q1_2_q, q2_1_q2_prime_j, q2_1_q2_prime_k, Q2_2_q;

  Q2 q2_1 (
    .Q2_prime_J(q2_1_q2_prime_j), .Q2(Q2_2_q), .Q1(Q1_2_q), .Q0(Q0_2_q), .x1(x1), .x0(x0),
    .Q2_prime_K(q2_1_q2_prime_k));
  Q1 q1_1 (
    .Q2(Q2_2_q), .Q1(Q1_2_q), .Q0(Q0_2_q), .x1(x1), .x0(x0), .Q1_prime_J(q1_1_q1_prime_j),
    .Q1_prime_K(q1_1_q1_prime_k));
  Q0 q0_1 (
    .Q2(Q2_2_q), .Q1(Q1_2_q), .Q0(Q0_2_q), .x1(x1), .x0(x0), .Q0_prime_J(q0_1_q0_prime_j),
    .Q0_prime_K(q0_1_q0_prime_k));
  Clock clock_1 (.out(clock_1_out));
  J_K_Flip_Flop Q2_2 (
    .J(q2_1_q2_prime_j), .clk(clock_1_out), .K(q2_1_q2_prime_k), .Q(Q2_2_q));  // open: Qn, preset, en, reset
  J_K_Flip_Flop Q1_2 (
    .J(q1_1_q1_prime_j), .clk(clock_1_out), .K(q1_1_q1_prime_k), .Q(Q1_2_q));  // open: Qn, preset, en, reset
  J_K_Flip_Flop Q0_2 (
    .J(q0_1_q0_prime_j), .clk(clock_1_out), .K(q0_1_q0_prime_k), .Q(Q0_2_q));  // open: Qn, preset, en, reset
  not not_1 (not_1_out, Q2_2_q);
  not not_2 (not_2_out, Q1_2_q);
  nand nand_1 (nand_1_out, not_1_out, not_2_out, Q0_2_q);
  not not_3 (y, nand_1_out);

  // Notes on the sheet:
  //   Bartłomiej Rasztabiga
endmodule

// Q2'
module Q2 (
  input  Q2,
  input  Q1,
  input  Q0,
  input  x1,
  input  x0,
  output Q2_prime_J,
  output Q2_prime_K
);

  wire nand_1_out, not_1_out, not_2_out;

  not not_1 (not_1_out, Q1);
  not not_2 (not_2_out, x0);
  nand nand_1 (nand_1_out, not_2_out, not_1_out);
  not not_3 (Q2_prime_J, nand_1_out);

  assign Q2_prime_K = 1'b1;
endmodule

// Q1'
module Q1 (
  input  Q2,
  input  Q1,
  input  Q0,
  input  x1,
  input  x0,
  output Q1_prime_J,
  output Q1_prime_K
);

  wire not_1_out, not_3_out, not_4_out;

  not not_1 (not_1_out, Q2);
  not not_2 (Q1_prime_J, x0);
  not not_3 (not_3_out, not_1_out);
  not not_4 (not_4_out, x0);
  nand nand_1 (Q1_prime_K, not_3_out, not_4_out);
endmodule

// Q0'
module Q0 (
  input  Q2,
  input  Q1,
  input  Q0,
  input  x1,
  input  x0,
  output Q0_prime_J,
  output Q0_prime_K
);

  wire nand_1_out, nand_2_out, not_1_out, not_2_out, not_3_out;

  not not_1 (not_1_out, Q2);
  not not_2 (not_2_out, x0);
  not not_3 (not_3_out, x1);
  nand nand_1 (nand_1_out, not_2_out, not_1_out, Q1);
  nand nand_2 (nand_2_out, not_3_out, not_2_out, Q1);
  nand nand_3 (Q0_prime_J, nand_1_out, nand_2_out);

  assign Q0_prime_K = 1'b1;
endmodule
