// Logisim project zad.circ as structural Verilog: 1 circuit, main circuit main
module main (
  input  SYNC,
  input  [3:0] \input ,
  output ACK,
  output WYN,
  output [3:0] y
);

  wire and_1_out, clock_1_out, multiplexer_2_out, nor_1_out, not_1_out, not_2_out, or_1_out, X_out;
  wire [2:0] LX_q, rom_1_data_2;
  wire [3:0] adder_1_out, counter_1_q, multiplexer_1_out;
  wire [12:0] rom_1_data;

  Clock clock_1 (.out(clock_1_out));
  Adder #(.width(4)) adder_1 (.a(y), .b(\input ), .out(adder_1_out));  // open: cin, cout
  Multiplexer #(.width(4), .enable("false")) multiplexer_1 (
    .in0(y), .in1(adder_1_out), .out(multiplexer_1_out), .sel(X_out));
  Register #(.width(4)) u_Y (.D(multiplexer_1_out), .en(rom_1_data[7]), .Q(y), .clk(clock_1_out), .clr(rom_1_data[6]));
  Shift_Register #(.length(4)) X (
    .clk(and_1_out), .out(X_out), .load(rom_1_data[4]), .d0(\input [0]), .d1(\input [1]), .d2(\input [2]),
    .d3(\input [3]));  // open: shift, in, clr, q0, q1, q2, q3
  and and_1 (and_1_out, clock_1_out, rom_1_data[5]);
  or or_1 (or_1_out, rom_1_data[11], rom_1_data[12]);
  Counter #(.width(3), .max('h7)) LX (
    .load(or_1_out), .D(3'b100), .count(rom_1_data[11]), .Q(LX_q), .clk(clock_1_out));  // open: carry, clr
  nor nor_1 (nor_1_out, LX_q[0], LX_q[1], LX_q[2]);
  not not_1 (not_1_out, SYNC);
  Multiplexer #(.select(3), .enable("false")) multiplexer_2 (
    .in0(SYNC), .in1(not_1_out), .in2(X_out), .in3(nor_1_out), .in4(1'b0), .in5(1'b0), .in6(1'b0),
    .in7(1'b0), .out(multiplexer_2_out), .sel(rom_1_data_2));
  not not_2 (not_2_out, multiplexer_2_out);
  Counter #(.width(4), .max('hf), .trigger("falling")) counter_1 (
    .load(not_2_out), .D(rom_1_data[3:0]), .count(multiplexer_2_out), .Q(counter_1_q), .clk(clock_1_out));  // open: carry, clr
  D_Flip_Flop #(.trigger("falling")) d_ff_1 (
    .clk(1'b0), .D(1'b0), .Q(ACK), .preset(rom_1_data[8]), .reset(rom_1_data[9]));  // open: Qn, en
  ROM #(.addrWidth(4), .dataWidth(16)) rom_1 (
    .addr(counter_1_q), .data({rom_1_data_2, rom_1_data[12:11], WYN, rom_1_data[9:0]}));  // open: sel

  // Notes on the sheet:
  //   contents of rom_1 (hex, n*v repeats v):
  //   1270 2101 202 4805 8095 6008 2506 8000 2108 8022
endmodule
