// Logisim project zad.circ as structural Verilog: 1 circuit, main circuit main
module main (
  input  SYNC,
  input  [3:0] \input ,
  output ACK,
  output WYN,
  output [3:0] y1,
  output [3:0] y0
);

  wire clock_1_out, comparator_1_gt, LX_carry, multiplexer_3_out, not_1_out, not_2_out, not_3_out, or_1_out;
  wire [0:0] comparator_2_lt;
  wire [1:0] rom_1_data_2;
  wire [2:0] counter_1_q;
  wire [3:0] multiplexer_1_out, multiplexer_2_out;
  wire [12:0] rom_1_data;

  Clock clock_1 (.out(clock_1_out));
  Comparator #(.width(4), .mode("unsigned")) comparator_1 (.a(\input ), .b(y1), .gt(comparator_1_gt));  // open: eq, lt
  Multiplexer #(.width(4), .enable("false")) multiplexer_1 (
    .in0(y1), .in1(\input ), .out(multiplexer_1_out), .sel(comparator_1_gt));
  Register #(.width(4)) Rmax (
    .D(multiplexer_1_out), .en(rom_1_data[6]), .Q(y1), .clk(clock_1_out), .clr(rom_1_data[5]));
  or or_1 (or_1_out, rom_1_data[4], rom_1_data[3]);
  Counter #(.width(4), .max('hf)) LX (
    .load(or_1_out), .D(\input ), .count(rom_1_data[3]), .carry(LX_carry), .clk(clock_1_out));  // open: Q, clr
  Multiplexer #(.select(2), .width(4), .enable("false")) multiplexer_2 (
    .in0(y0), .in1(\input ), .in2(4'b1111), .in3(4'b1111), .out(multiplexer_2_out),
    .sel({rom_1_data[7], comparator_2_lt[0]}));
  Comparator #(.width(4), .mode("unsigned")) comparator_2 (
    .a(\input ), .b(y0), .lt(comparator_2_lt[0]));  // open: gt, eq
  Register #(.width(4)) Rmin (.D(multiplexer_2_out), .en(rom_1_data[8]), .Q(y0), .clk(clock_1_out));  // open: clr
  not not_1 (not_1_out, SYNC);
  D_Flip_Flop d_ff_1 (.clk(1'b0), .D(1'b0), .Q(ACK), .preset(rom_1_data[9]), .reset(rom_1_data[10]));  // open: Qn, en
  D_Flip_Flop d_ff_2 (.clk(1'b0), .D(1'b0), .Q(WYN), .preset(rom_1_data[11]), .reset(rom_1_data[12]));  // open: Qn, en
  Multiplexer #(.select(2), .enable("false")) multiplexer_3 (
    .in0(SYNC), .in1(not_1_out), .in2(not_2_out), .in3(1'b0), .out(multiplexer_3_out), .sel(rom_1_data_2));
  not not_2 (not_2_out, LX_carry);
  not not_3 (not_3_out, multiplexer_3_out);
  Counter #(.width(3), .max('h7), .trigger("falling")) counter_1 (
    .load(not_3_out), .D(rom_1_data[2:0]), .count(multiplexer_3_out), .Q(counter_1_q), .clk(clock_1_out));  // open: carry, clr
  ROM #(.addrWidth(3), .dataWidth(15)) rom_1 (.addr(counter_1_q), .data({rom_1_data_2, rom_1_data}));  // open: sel
endmodule
