// Logisim project przyklad_apn.circ as structural Verilog: 1 circuit, main circuit main
module main (
  input  x4,
  input  x3,
  input  x2,
  input  x1,
  input  x0,
  output y
);

  wire nand_1_out, nand_2_out, nand_3_out, nand_4_out, nand_5_out, not_1_out, not_2_out, not_3_out,
       not_4_out, not_5_out;

  not not_1 (not_1_out, x4);
  not not_2 (not_2_out, x3);
  not not_3 (not_3_out, x2);
  not not_4 (not_4_out, x1);
  not not_5 (not_5_out, x0);
  nand nand_1 (nand_1_out, x4, x3, not_3_out);
  nand nand_2 (nand_2_out, not_2_out, x2, x1);
  nand nand_3 (nand_3_out, not_1_out, not_2_out, not_3_out, not_4_out, not_5_out);
  nand nand_4 (nand_4_out, x3, x2, not_4_out);
  nand nand_5 (nand_5_out, x4, not_2_out, x2, x0);
  nand nand_6 (y, nand_1_out, nand_2_out, nand_3_out, nand_4_out, nand_5_out);
endmodule
