// Logisim project przyklad_async.circ as structural Verilog: 4 circuits, main circuit main
module main (
  input  a,
  input  b,
  output y
);

  wire clock_1_out, d_ff_1_q, d_ff_2_q, d_ff_3_q, nand_1_out, nand_2_out, nand_3_out, nand_4_out, nand_5_out,
       nand_6_out, nand_7_out, nand_8_out, nand_9_out, nand_10_out, nand_11_out, nand_12_out, nand_13_out,
       nand_14_out, nand_15_out, nand_16_out, nand_17_out, nand_18_out, nand_19_out, not_1_out, not_2_out,
       not_3_out, not_4_out, not_5_out, not_6_out, not_7_out, not_8_out;

  not not_1 (not_1_out, a);
  not not_2 (not_2_out, b);
  not not_3 (not_3_out, d_ff_2_q);
  not not_4 (not_4_out, d_ff_1_q);
  not not_5 (not_5_out, d_ff_3_q);
  nand nand_1 (nand_1_out, a, not_2_out, not_5_out);
  nand nand_2 (nand_2_out, a, not_2_out, d_ff_1_q);
  nand nand_3 (nand_3_out, b, d_ff_1_q, d_ff_3_q);
  nand nand_4 (nand_4_out, not_1_out, d_ff_2_q);
  nand nand_5 (nand_5_out, d_ff_1_q, not_5_out);
  not not_6 (not_6_out, d_ff_2_q);
  nand nand_6 (nand_6_out, a, not_2_out, not_4_out, d_ff_3_q);
  nand nand_7 (nand_7_out, not_1_out, not_2_out);
  nand nand_8 (nand_8_out, a, d_ff_2_q, not_5_out);
  nand nand_9 (nand_9_out, a, not_2_out, d_ff_2_q);
  nand nand_10 (nand_10_out, a, b, d_ff_3_q);
  nand nand_11 (nand_11_out, a, b, d_ff_2_q);
  nand nand_12 (nand_12_out, a, not_4_out, d_ff_3_q);
  nand nand_13 (nand_13_out, a, b, not_4_out, not_3_out);
  nand nand_14 (nand_14_out, nand_1_out, nand_2_out, nand_3_out, nand_4_out, nand_5_out, not_6_out);
  nand nand_15 (nand_15_out, nand_6_out, nand_7_out, nand_8_out, nand_9_out);
  nand nand_16 (nand_16_out, nand_10_out, nand_11_out, nand_12_out, nand_13_out);
  Clock clock_1 (.out(clock_1_out));
  LED Q2 (.in(d_ff_1_q));
  D_Flip_Flop d_ff_1 (.clk(clock_1_out), .D(nand_14_out), .Q(d_ff_1_q));  // open: Qn, preset, en, reset
  D_Flip_Flop d_ff_2 (.clk(clock_1_out), .D(nand_15_out), .Q(d_ff_2_q));  // open: Qn, preset, en, reset
  D_Flip_Flop d_ff_3 (.clk(clock_1_out), .D(nand_16_out), .Q(d_ff_3_q));  // open: Qn, preset, en, reset
  LED Q1 (.in(d_ff_2_q));
  LED Q0 (.in(d_ff_3_q));
  not not_7 (not_7_out, d_ff_1_q);
  not not_8 (not_8_out, d_ff_3_q);
  nand nand_17 (nand_17_out, not_7_out, not_8_out);
  nand nand_18 (nand_18_out, d_ff_2_q, not_8_out);
  nand nand_19 (nand_19_out, d_ff_1_q, d_ff_3_q);
  nand nand_20 (y, nand_17_out, nand_18_out, nand_19_out);
endmodule

// Q2'
module Q2 (
  input  Q2,
  input  Q1,
  input  Q0,
  input  x,
  input  x0,
  output Q2_prime
);

  wire nand_1_out, nand_2_out, nand_3_out, not_1_out, not_2_out, not_3_out, not_4_out;

  not not_1 (not_1_out, Q2);
  not not_2 (not_2_out, Q0);
  not not_3 (not_3_out, x);
  not not_4 (not_4_out, x0);
  nand nand_1 (nand_1_out, not_3_out, not_1_out, Q0);
  nand nand_2 (nand_2_out, not_1_out, Q1);
  nand nand_3 (nand_3_out, Q1, not_2_out);
  nand nand_4 (Q2_prime, nand_1_out, nand_2_out, nand_3_out, not_4_out);
endmodule

// Q1'
module Q1 (
  input  Q2,
  input  Q1,
  input  Q0,
  input  x,
  input  x0,
  output Q1_prime
);

  wire nand_1_out, nand_2_out, nand_3_out, not_1_out, not_2_out, not_3_out, not_4_out, not_5_out;

  not not_1 (not_1_out, Q2);
  not not_2 (not_2_out, Q0);
  not not_3 (not_3_out, Q1);
  not not_4 (not_4_out, x);
  not not_5 (not_5_out, x0);
  nand nand_1 (nand_1_out, not_1_out, Q0);
  nand nand_2 (nand_2_out, not_4_out, Q2, not_2_out);
  nand nand_3 (nand_3_out, not_1_out, not_3_out);
  nand nand_4 (Q1_prime, nand_1_out, nand_2_out, nand_3_out, not_5_out);
endmodule

// Q0'
module Q0 (
  input  Q2,
  input  Q1,
  input  Q0,
  input  x,
  input  x0,
  output Q0_prime
);

  wire nand_1_out, nand_2_out, nand_3_out, nand_4_out, not_1_out, not_2_out, not_3_out, not_4_out;

  not not_1 (not_1_out, Q2);
  not not_2 (not_2_out, Q0);
  not not_3 (not_3_out, x);
  not not_4 (not_4_out, x0);
  nand nand_1 (nand_1_out, not_3_out, not_2_out);
  nand nand_2 (nand_2_out, not_1_out, Q1);
  nand nand_3 (nand_3_out, x, Q0);
  nand nand_4 (nand_4_out, Q1, not_2_out);
  nand nand_5 (Q0_prime, nand_1_out, nand_2_out, nand_3_out, nand_4_out, not_4_out);
endmodule
