// Logisim project przyklad_async2nieRnieS.circ as structural Verilog: 4 circuits, main circuit main
module main (
  input  a,
  input  b,
  output y
);

  wire and_1_out, and_2_out, and_3_out, and_4_out, and_5_out, and_6_out, and_7_out, and_8_out, d_ff_1_q,
       d_ff_1_qn, d_ff_2_q, d_ff_2_qn, d_ff_3_q, d_ff_3_qn, not_1_out, not_2_out, not_3_out, not_4_out,
       not_5_out, not_6_out, not_7_out, not_8_out, not_9_out, not_10_out, not_11_out, or_1_out, or_2_out,
       or_3_out, or_4_out, or_5_out;

  not not_1 (not_1_out, a);
  not not_2 (not_2_out, b);
  not not_3 (not_3_out, d_ff_2_q);
  not not_4 (not_4_out, d_ff_1_q);
  not not_5 (not_5_out, d_ff_3_q);
  and and_1 (and_1_out, not_5_out, not_2_out);
  and and_2 (and_2_out, d_ff_3_q, b);
  and and_3 (and_3_out, not_5_out, not_1_out);
  and and_4 (and_4_out, not_4_out, a);
  or or_1 (or_1_out, not_3_out, not_5_out, not_1_out, not_2_out);
  and and_5 (and_5_out, a, b);
  or or_2 (or_2_out, and_1_out, and_2_out, and_3_out);
  or or_3 (or_3_out, not_2_out, and_4_out);
  or or_4 (or_4_out, not_1_out, b);
  or or_5 (or_5_out, not_1_out, not_2_out, d_ff_1_q, d_ff_2_q);
  D_Flip_Flop d_ff_1 (
    .clk(1'b0), .D(1'b0), .Q(d_ff_1_q), .Qn(d_ff_1_qn), .preset(not_7_out), .reset(not_6_out));  // open: en
  not not_6 (not_6_out, and_5_out);
  not not_7 (not_7_out, or_1_out);
  D_Flip_Flop d_ff_2 (
    .clk(1'b0), .D(1'b0), .Q(d_ff_2_q), .Qn(d_ff_2_qn), .preset(not_9_out), .reset(not_8_out));  // open: en
  not not_8 (not_8_out, or_3_out);
  not not_9 (not_9_out, or_2_out);
  D_Flip_Flop d_ff_3 (
    .clk(1'b0), .D(1'b0), .Q(d_ff_3_q), .Qn(d_ff_3_qn), .preset(not_11_out), .reset(not_10_out));  // open: en
  not not_10 (not_10_out, or_5_out);
  not not_11 (not_11_out, or_4_out);
  LED Q2 (.in(d_ff_1_q));
  LED Q1 (.in(d_ff_2_q));
  LED Q0 (.in(d_ff_3_q));
  and and_6 (and_6_out, d_ff_1_qn, d_ff_2_qn, d_ff_3_qn);
  and and_7 (and_7_out, d_ff_3_q, d_ff_2_q);
  and and_8 (and_8_out, d_ff_3_q, d_ff_1_q);
  or or_6 (y, and_6_out, and_7_out, and_8_out);
endmodule

// Q2'
module Q2 (
  input  Q2,
  input  Q1,
  input  Q0,
  input  x,
  input  x0,
  output Q2_prime
);

  wire nand_1_out, nand_2_out, nand_3_out, not_1_out, not_2_out, not_3_out, not_4_out;

  not not_1 (not_1_out, Q2);
  not not_2 (not_2_out, Q0);
  not not_3 (not_3_out, x);
  not not_4 (not_4_out, x0);
  nand nand_1 (nand_1_out, not_3_out, not_1_out, Q0);
  nand nand_2 (nand_2_out, not_1_out, Q1);
  nand nand_3 (nand_3_out, Q1, not_2_out);
  nand nand_4 (Q2_prime, nand_1_out, nand_2_out, nand_3_out, not_4_out);
endmodule

// Q1'
module Q1 (
  input  Q2,
  input  Q1,
  input  Q0,
  input  x,
  input  x0,
  output Q1_prime
);

  wire nand_1_out, nand_2_out, nand_3_out, not_1_out, not_2_out, not_3_out, not_4_out, not_5_out;

  not not_1 (not_1_out, Q2);
  not not_2 (not_2_out, Q1);
  not not_3 (not_3_out, Q0);
  not not_4 (not_4_out, x);
  not not_5 (not_5_out, x0);
  nand nand_1 (nand_1_out, not_1_out, Q0);
  nand nand_2 (nand_2_out, not_4_out, Q2, not_3_out);
  nand nand_3 (nand_3_out, not_1_out, not_2_out);
  nand nand_4 (Q1_prime, nand_1_out, nand_2_out, nand_3_out, not_5_out);
endmodule

// Q0'
module Q0 (
  input  Q2,
  input  Q1,
  input  Q0,
  input  x,
  input  x0,
  output Q0_prime
);

  wire nand_1_out, nand_2_out, nand_3_out, nand_4_out, not_1_out, not_2_out, not_3_out, not_4_out;

  not not_1 (not_1_out, Q2);
  not not_2 (not_2_out, Q0);
  not not_3 (not_3_out, x);
  not not_4 (not_4_out, x0);
  nand nand_1 (nand_1_out, not_3_out, not_2_out);
  nand nand_2 (nand_2_out, not_1_out, Q1);
  nand nand_3 (nand_3_out, x, Q0);
  nand nand_4 (nand_4_out, Q1, not_2_out);
  nand nand_5 (Q0_prime, nand_1_out, nand_2_out, nand_3_out, nand_4_out, not_4_out);
endmodule
