// Logisim project przyklad_automat.circ as structural Verilog: 1 circuit, main circuit main
module main (
);

  wire and_1_out, and_2_out, and_3_out, and_4_out, clock_1_out, D0_q, D1_q, D2_q, not_1_out, not_2_out,
       not_3_out, or_1_out;

  Clock clock_1 (.out(clock_1_out));
  not not_1 (not_1_out, D2_q);
  not not_2 (not_2_out, D1_q);
  not not_3 (not_3_out, D0_q);
  and and_1 (and_1_out, not_1_out, D1_q, D0_q);
  and and_2 (and_2_out, not_1_out, D1_q, not_3_out);
  and and_3 (and_3_out, not_1_out, not_2_out, D0_q);
  and and_4 (and_4_out, not_1_out, not_3_out);
  or or_1 (or_1_out, and_2_out, and_3_out);
  D_Flip_Flop D2 (.clk(clock_1_out), .D(and_1_out), .Q(D2_q));  // open: Qn, preset, en, reset
  D_Flip_Flop D1 (.clk(clock_1_out), .D(or_1_out), .Q(D1_q));  // open: Qn, preset, en, reset
  D_Flip_Flop D0 (.clk(clock_1_out), .D(and_4_out), .Q(D0_q));  // open: Qn, preset, en, reset
endmodule
