// Logisim project przyklad_automat_B1.circ as structural Verilog: 1 circuit, main circuit main
module main (
  input  x,
  input  z,
  input  RES
);

  wire and_1_out, and_2_out, and_3_out, and_4_out, and_5_out, and_6_out, and_7_out, and_8_out, and_9_out,
       and_10_out, clock_1_out, D0_qn, D1_q, D1_qn, D2_q, D2_qn, not_1_out, not_2_out, or_1_out, or_2_out,
       or_3_out;

  not not_1 (not_1_out, x);
  not not_2 (not_2_out, z);
  Clock clock_1 (.out(clock_1_out));
  and and_1 (and_1_out, D1_qn, x);
  and and_2 (and_2_out, D2_qn, D1_q);
  and and_3 (and_3_out, D2_q, D1_qn);
  and and_4 (and_4_out, D1_qn, not_1_out);
  and and_5 (and_5_out, D2_qn, D1_q);
  and and_6 (and_6_out, D2_q, D1_qn);
  and and_7 (and_7_out, D2_qn, D0_qn, not_2_out);
  and and_8 (and_8_out, D2_qn, D1_qn, x, not_2_out);
  and and_9 (and_9_out, D2_q, D1_qn, not_1_out, not_2_out);
  and and_10 (and_10_out, D2_q, D1_q, x, not_2_out);
  or or_1 (or_1_out, and_1_out, and_2_out, and_3_out, z);
  or or_2 (or_2_out, and_4_out, and_5_out, and_6_out, z);
  or or_3 (or_3_out, and_7_out, and_8_out, and_9_out, and_10_out);
  D_Flip_Flop D2 (.clk(clock_1_out), .D(or_1_out), .Q(D2_q), .Qn(D2_qn), .reset(RES));  // open: preset, en
  D_Flip_Flop D1 (.clk(clock_1_out), .D(or_2_out), .Q(D1_q), .Qn(D1_qn), .reset(RES));  // open: preset, en
  D_Flip_Flop D0 (.clk(clock_1_out), .D(or_3_out), .Qn(D0_qn), .reset(RES));  // open: Q, preset, en
endmodule
