// Logisim project przyklad_automat_B3.circ as structural Verilog: 4 circuits, main circuit main
module main (
);

  wire and_1_out, and_2_out, and_3_out, and_4_out, clock_1_out, s_r_ff_1_q, s_r_ff_1_qn, s_r_ff_2_q,
       s_r_ff_2_qn, s_r_ff_3_q, s_r_ff_3_qn;

  and and_1 (and_1_out, s_r_ff_2_q, s_r_ff_3_q);
  and and_2 (and_2_out, s_r_ff_2_qn, s_r_ff_3_q);
  and and_3 (and_3_out, s_r_ff_2_q, s_r_ff_3_q);
  and and_4 (and_4_out, s_r_ff_1_qn, s_r_ff_3_qn);
  Clock clock_1 (.out(clock_1_out));
  S_R_Flip_Flop s_r_ff_1 (
    .S(and_1_out), .clk(clock_1_out), .R(s_r_ff_2_qn), .Q(s_r_ff_1_q), .Qn(s_r_ff_1_qn));  // open: preset, reset, en
  S_R_Flip_Flop s_r_ff_2 (
    .S(and_2_out), .clk(clock_1_out), .R(and_3_out), .Q(s_r_ff_2_q), .Qn(s_r_ff_2_qn));  // open: preset, reset, en
  S_R_Flip_Flop s_r_ff_3 (
    .S(and_4_out), .clk(clock_1_out), .R(s_r_ff_3_q), .Q(s_r_ff_3_q), .Qn(s_r_ff_3_qn));  // open: preset, reset, en
  LED led_1 (.in(s_r_ff_1_q));
  LED led_2 (.in(s_r_ff_2_q));
  LED led_3 (.in(s_r_ff_3_q));
endmodule

// Q2'
module Q2 (
  input  Q2,
  input  Q1,
  input  Q0,
  input  x,
  input  x0,
  output Q2_prime
);

  wire nand_1_out, nand_2_out, nand_3_out, not_1_out, not_2_out, not_3_out, not_4_out;

  not not_1 (not_1_out, Q2);
  not not_2 (not_2_out, Q0);
  not not_3 (not_3_out, x);
  not not_4 (not_4_out, x0);
  nand nand_1 (nand_1_out, not_3_out, not_1_out, Q0);
  nand nand_2 (nand_2_out, not_1_out, Q1);
  nand nand_3 (nand_3_out, Q1, not_2_out);
  nand nand_4 (Q2_prime, nand_1_out, nand_2_out, nand_3_out, not_4_out);
endmodule

// Q1'
module Q1 (
  input  Q2,
  input  Q1,
  input  Q0,
  input  x,
  input  x0,
  output Q1_prime
);

  wire nand_1_out, nand_2_out, nand_3_out, not_1_out, not_2_out, not_3_out, not_4_out, not_5_out;

  not not_1 (not_1_out, Q2);
  not not_2 (not_2_out, Q1);
  not not_3 (not_3_out, Q0);
  not not_4 (not_4_out, x);
  not not_5 (not_5_out, x0);
  nand nand_1 (nand_1_out, not_1_out, Q0);
  nand nand_2 (nand_2_out, not_4_out, Q2, not_3_out);
  nand nand_3 (nand_3_out, not_1_out, not_2_out);
  nand nand_4 (Q1_prime, nand_1_out, nand_2_out, nand_3_out, not_5_out);
endmodule

// Q0'
module Q0 (
  input  Q2,
  input  Q1,
  input  Q0,
  input  x,
  input  x0,
  output Q0_prime
);

  wire nand_1_out, nand_2_out, nand_3_out, nand_4_out, not_1_out, not_2_out, not_3_out, not_4_out;

  not not_1 (not_1_out, Q2);
  not not_2 (not_2_out, Q0);
  not not_3 (not_3_out, x);
  not not_4 (not_4_out, x0);
  nand nand_1 (nand_1_out, not_3_out, not_2_out);
  nand nand_2 (nand_2_out, not_1_out, Q1);
  nand nand_3 (nand_3_out, x, Q0);
  nand nand_4 (nand_4_out, Q1, not_2_out);
  nand nand_5 (Q0_prime, nand_1_out, nand_2_out, nand_3_out, nand_4_out, not_4_out);
endmodule
