// Logisim project przyklad_automat_RS.circ as structural Verilog: 1 circuit, main circuit main
module main (
  input  x1,
  input  x0
);

  wire and_1_out, and_2_out, and_3_out, and_4_out, and_5_out, and_6_out, and_7_out, and_8_out, and_9_out,
       clock_1_out, L0_q, L0_qn, L1_q, L1_qn, not_1_out, not_2_out, or_1_out, or_2_out, or_3_out, or_4_out;

  not not_1 (not_1_out, x1);
  not not_2 (not_2_out, x0);
  and and_1 (and_1_out, L1_qn, x0);
  and and_2 (and_2_out, L1_qn, x1);
  and and_3 (and_3_out, L1_q, not_1_out);
  and and_4 (and_4_out, L1_q, not_2_out);
  and and_5 (and_5_out, L1_qn, L0_qn, not_1_out, x0);
  and and_6 (and_6_out, L1_q, L0_qn, x1, not_2_out);
  and and_7 (and_7_out, not_1_out, not_2_out);
  and and_8 (and_8_out, L1_qn, L0_q, x0);
  and and_9 (and_9_out, L1_q, L0_q, x1);
  or or_1 (or_1_out, and_1_out, and_2_out);
  or or_2 (or_2_out, and_3_out, and_4_out);
  or or_3 (or_3_out, and_5_out, and_6_out);
  or or_4 (or_4_out, and_7_out, and_8_out, and_9_out);
  Clock clock_1 (.out(clock_1_out));
  S_R_Flip_Flop L1 (.S(or_1_out), .clk(clock_1_out), .R(or_2_out), .Q(L1_q), .Qn(L1_qn));  // open: preset, reset, en
  S_R_Flip_Flop L0 (.S(or_3_out), .clk(clock_1_out), .R(or_4_out), .Q(L0_q), .Qn(L0_qn));  // open: preset, reset, en
endmodule
