// Logisim project przyklad_automat_lab3_D.circ as structural Verilog: 4 circuits, main circuit main
module main (
  input  x,
  input  x0,
  output y
);

  wire clock_1_out, nand_1_out, q0_1_q0_prime, Q0_2_q, q1_1_q1_prime, Q1_2_q, q2_1_q2_prime, Q2_2_q;

  Q2 q2_1 (.Q2_prime(q2_1_q2_prime), .Q2(Q2_2_q), .Q1(Q1_2_q), .Q0(Q0_2_q), .x(x), .x0(x0));
  Q1 q1_1 (.Q1_prime(q1_1_q1_prime), .Q2(Q2_2_q), .Q1(Q1_2_q), .Q0(Q0_2_q), .x(x), .x0(x0));
  Q0 q0_1 (.Q0_prime(q0_1_q0_prime), .Q2(Q2_2_q), .Q1(Q1_2_q), .Q0(Q0_2_q), .x(x), .x0(x0));
  Clock clock_1 (.out(clock_1_out));
  D_Flip_Flop Q2_2 (.clk(clock_1_out), .D(q2_1_q2_prime), .Q(Q2_2_q));  // open: Qn, preset, en, reset
  D_Flip_Flop Q1_2 (.clk(clock_1_out), .D(q1_1_q1_prime), .Q(Q1_2_q));  // open: Qn, preset, en, reset
  D_Flip_Flop Q0_2 (.clk(clock_1_out), .D(q0_1_q0_prime), .Q(Q0_2_q));  // open: Qn, preset, en, reset
  nand nand_1 (nand_1_out, Q2_2_q, Q1_2_q, Q0_2_q);
  not not_1 (y, nand_1_out);
endmodule

// Q2'
module Q2 (
  input  Q2,
  input  Q1,
  input  Q0,
  input  x,
  input  x0,
  output Q2_prime
);

  wire nand_1_out, nand_2_out, nand_3_out, not_1_out, not_2_out, not_3_out, not_4_out;

  not not_1 (not_1_out, Q2);
  not not_2 (not_2_out, Q0);
  not not_3 (not_3_out, x);
  not not_4 (not_4_out, x0);
  nand nand_1 (nand_1_out, not_3_out, not_1_out, Q0);
  nand nand_2 (nand_2_out, not_1_out, Q1);
  nand nand_3 (nand_3_out, Q1, not_2_out);
  nand nand_4 (Q2_prime, nand_1_out, nand_2_out, nand_3_out, not_4_out);
endmodule

// Q1'
module Q1 (
  input  Q2,
  input  Q1,
  input  Q0,
  input  x,
  input  x0,
  output Q1_prime
);

  wire nand_1_out, nand_2_out, nand_3_out, not_1_out, not_2_out, not_3_out, not_4_out, not_5_out;

  not not_1 (not_1_out, Q2);
  not not_2 (not_2_out, Q1);
  not not_3 (not_3_out, Q0);
  not not_4 (not_4_out, x);
  not not_5 (not_5_out, x0);
  nand nand_1 (nand_1_out, not_1_out, Q0);
  nand nand_2 (nand_2_out, not_4_out, Q2, not_3_out);
  nand nand_3 (nand_3_out, not_1_out, not_2_out);
  nand nand_4 (Q1_prime, nand_1_out, nand_2_out, nand_3_out, not_5_out);
endmodule

// Q0'
module Q0 (
  input  Q2,
  input  Q1,
  input  Q0,
  input  x,
  input  x0,
  output Q0_prime
);

  wire nand_1_out, nand_2_out, nand_3_out, nand_4_out, not_1_out, not_2_out, not_3_out, not_4_out;

  not not_1 (not_1_out, Q2);
  not not_2 (not_2_out, Q0);
  not not_3 (not_3_out, x);
  not not_4 (not_4_out, x0);
  nand nand_1 (nand_1_out, not_3_out, not_2_out);
  nand nand_2 (nand_2_out, not_1_out, Q1);
  nand nand_3 (nand_3_out, x, Q0);
  nand nand_4 (nand_4_out, Q1, not_2_out);
  nand nand_5 (Q0_prime, nand_1_out, nand_2_out, nand_3_out, nand_4_out, not_4_out);
endmodule
