// Logisim project przyklad_automat_lab3_JK.circ as structural Verilog: 4 circuits, main circuit main
module main (
  input  x,
  input  x0,
  output y
);

  wire clock_1_out, j_k_ff_1_q, nand_1_out, q0_1_q0_prime, Q0_2_q, q1_1_q1_prime, Q1_2_q, q2_1_q2_prime_j,
       q2_1_q2_prime_k;

  Q2 q2_1 (
    .Q2_prime_J(q2_1_q2_prime_j), .Q2(j_k_ff_1_q), .Q1(Q1_2_q), .Q0(Q0_2_q), .x(x), .x0(x0),
    .Q2_prime_K(q2_1_q2_prime_k));
  Q1 q1_1 (.Q1_prime(q1_1_q1_prime), .Q2(j_k_ff_1_q), .Q1(Q1_2_q), .Q0(Q0_2_q), .x(x), .x0(x0));
  Q0 q0_1 (.Q0_prime(q0_1_q0_prime), .Q2(j_k_ff_1_q), .Q1(Q1_2_q), .Q0(Q0_2_q), .x(x), .x0(x0));
  Clock clock_1 (.out(clock_1_out));
  J_K_Flip_Flop j_k_ff_1 (
    .J(q2_1_q2_prime_j), .clk(clock_1_out), .K(q2_1_q2_prime_k), .Q(j_k_ff_1_q));  // open: Qn, preset, en, reset
  D_Flip_Flop Q1_2 (.clk(clock_1_out), .D(q1_1_q1_prime), .Q(Q1_2_q));  // open: Qn, preset, en, reset
  D_Flip_Flop Q0_2 (.clk(clock_1_out), .D(q0_1_q0_prime), .Q(Q0_2_q));  // open: Qn, preset, en, reset
  not not_1 (y, nand_1_out);
  nand nand_1 (nand_1_out, j_k_ff_1_q, Q1_2_q, Q0_2_q);
endmodule

// Q2'
module Q2 (
  input  Q2,
  input  Q1,
  input  Q0,
  input  x,
  input  x0,
  output Q2_prime_J,
  output Q2_prime_K
);

  wire nand_1_out, nand_2_out, not_1_out, not_2_out, not_3_out, not_4_out;

  not not_1 (not_1_out, x0);
  not not_2 (not_2_out, x);
  not not_3 (not_3_out, Q1);
  not not_4 (not_4_out, x0);
  nand nand_1 (nand_1_out, not_2_out, Q0);
  nand nand_2 (nand_2_out, not_1_out, Q0);
  nand nand_3 (Q2_prime_J, nand_1_out, not_3_out, not_4_out);
  not not_5 (Q2_prime_K, nand_2_out);
endmodule

// Q1'
module Q1 (
  input  Q2,
  input  Q1,
  input  Q0,
  input  x,
  input  x0,
  output Q1_prime
);

  wire nand_1_out, nand_2_out, nand_3_out, not_1_out, not_2_out, not_3_out, not_4_out, not_5_out;

  not not_1 (not_1_out, Q2);
  not not_2 (not_2_out, Q1);
  not not_3 (not_3_out, Q0);
  not not_4 (not_4_out, x);
  not not_5 (not_5_out, x0);
  nand nand_1 (nand_1_out, not_1_out, Q0);
  nand nand_2 (nand_2_out, not_4_out, Q2, not_3_out);
  nand nand_3 (nand_3_out, not_1_out, not_2_out);
  nand nand_4 (Q1_prime, nand_1_out, nand_2_out, nand_3_out, not_5_out);
endmodule

// Q0'
module Q0 (
  input  Q2,
  input  Q1,
  input  Q0,
  input  x,
  input  x0,
  output Q0_prime
);

  wire nand_1_out, nand_2_out, nand_3_out, nand_4_out, not_1_out, not_2_out, not_3_out, not_4_out;

  not not_1 (not_1_out, Q2);
  not not_2 (not_2_out, Q0);
  not not_3 (not_3_out, x);
  not not_4 (not_4_out, x0);
  nand nand_1 (nand_1_out, not_3_out, not_2_out);
  nand nand_2 (nand_2_out, not_1_out, Q1);
  nand nand_3 (nand_3_out, x, Q0);
  nand nand_4 (nand_4_out, Q1, not_2_out);
  nand nand_5 (Q0_prime, nand_1_out, nand_2_out, nand_3_out, nand_4_out, not_4_out);
endmodule
