// Logisim project przyklad_automat_lab3_JK2.circ as structural Verilog: 4 circuits, main circuit main
module main (
  input  a,
  input  b,
  output y
);

  wire clock_1_out, nand_1_out, nand_2_out, nand_3_out, nand_4_out, nand_5_out, nand_6_out, nand_7_out,
       nand_8_out, nand_9_out, nand_10_out, nand_11_out, nand_12_out, not_1_out, not_2_out, not_3_out,
       not_4_out, Q0_q, Q0_qn, Q1_qn, Q2_q, Q2_qn;

  not not_1 (not_1_out, a);
  not not_2 (not_2_out, b);
  not not_3 (not_3_out, nand_1_out);
  nand nand_1 (nand_1_out, y, Q0_qn, not_1_out, b);
  nand nand_2 (nand_2_out, Q0_qn, not_1_out, not_2_out);
  nand nand_3 (nand_3_out, a, b);
  nand nand_4 (nand_4_out, Q0_q, a);
  nand nand_5 (nand_5_out, Q1_qn, b);
  nand nand_6 (nand_6_out, y, not_2_out);
  nand nand_7 (nand_7_out, not_1_out, not_2_out);
  nand nand_8 (nand_8_out, Q0_qn, a, b);
  nand nand_9 (nand_9_out, Q0_q, not_1_out);
  nand nand_10 (nand_10_out, nand_5_out, nand_6_out);
  not not_4 (not_4_out, nand_7_out);
  nand nand_11 (nand_11_out, nand_8_out, nand_9_out);
  nand nand_12 (nand_12_out, nand_2_out, nand_3_out, nand_4_out);
  Clock clock_1 (.out(clock_1_out));
  J_K_Flip_Flop Q2 (.J(not_3_out), .clk(clock_1_out), .K(1'b1), .Q(Q2_q), .Qn(Q2_qn));  // open: preset, en, reset
  J_K_Flip_Flop Q1 (.J(nand_11_out), .clk(clock_1_out), .K(nand_12_out), .Q(y), .Qn(Q1_qn));  // open: preset, en, reset
  J_K_Flip_Flop Q0 (
    .J(nand_10_out), .clk(clock_1_out), .K(not_4_out), .Q(Q0_q), .Qn(Q0_qn));  // open: preset, en, reset
endmodule

// Q2'
module Q2 (
  input  Q2,
  input  Q1,
  input  Q0,
  input  x,
  input  x0,
  output Q2_prime_J,
  output Q2_prime_K
);
endmodule

// Q1'
module Q1 (
  input  Q2,
  input  Q1,
  input  Q0,
  input  x,
  input  x0,
  output Q1_prime
);

  wire nand_1_out, nand_2_out, nand_3_out, not_1_out, not_2_out, not_3_out, not_4_out, not_5_out;

  not not_1 (not_1_out, Q2);
  not not_2 (not_2_out, Q0);
  not not_3 (not_3_out, Q1);
  not not_4 (not_4_out, x);
  not not_5 (not_5_out, x0);
  nand nand_1 (nand_1_out, not_1_out, Q0);
  nand nand_2 (nand_2_out, not_4_out, Q2, not_2_out);
  nand nand_3 (nand_3_out, not_1_out, not_3_out);
  nand nand_4 (Q1_prime, nand_1_out, nand_2_out, nand_3_out, not_5_out);
endmodule

// Q0'
module Q0 (
  input  Q2,
  input  Q1,
  input  Q0,
  input  x,
  input  x0,
  output Q0_prime
);

  wire nand_1_out, nand_2_out, nand_3_out, nand_4_out, not_1_out, not_2_out, not_3_out, not_4_out;

  not not_1 (not_1_out, Q2);
  not not_2 (not_2_out, Q0);
  not not_3 (not_3_out, x);
  not not_4 (not_4_out, x0);
  nand nand_1 (nand_1_out, not_3_out, not_2_out);
  nand nand_2 (nand_2_out, not_1_out, Q1);
  nand nand_3 (nand_3_out, x, Q0);
  nand nand_4 (nand_4_out, Q1, not_2_out);
  nand nand_5 (Q0_prime, nand_1_out, nand_2_out, nand_3_out, nand_4_out, not_4_out);
endmodule
