// Logisim project przyklad_iteracyjny_A1.circ as structural Verilog: 2 circuits, main circuit main
module main (
  input  xi,
  input  xi_2,
  input  xi_3,
  input  xi_4,
  input  xi_5,
  input  xi_6,
  input  xi_7,
  input  xi_8,
  output out_9,
  output out_10,
  output out_11,
  output out_12,
  output out_13,
  output out_14,
  output out_15,
  output out_16
);

  wire blok_1_p__i_1, blok_1_p__i_1_2, blok_2_p__i_1, blok_2_p__i_1_2, blok_3_p__i_1, blok_3_p__i_1_2,
       blok_4_p__i_1, blok_4_p__i_1_2, blok_5_p__i_1, blok_5_p__i_1_2, blok_6_p__i_1, blok_6_p__i_1_2,
       blok_7_p__i_1, blok_7_p__i_1_2;

  blok blok_1 (.x__i(xi), .p__i(1'b0), .q__i(1'b0), .y__i(out_9), .p__i_1(blok_1_p__i_1), .p__i_1_2(blok_1_p__i_1_2));
  blok blok_2 (
    .x__i(xi_2), .p__i(blok_1_p__i_1), .q__i(blok_1_p__i_1_2), .y__i(out_10), .p__i_1(blok_2_p__i_1),
    .p__i_1_2(blok_2_p__i_1_2));
  blok blok_3 (
    .x__i(xi_3), .p__i(blok_2_p__i_1), .q__i(blok_2_p__i_1_2), .y__i(out_11), .p__i_1(blok_3_p__i_1),
    .p__i_1_2(blok_3_p__i_1_2));
  blok blok_4 (
    .x__i(xi_4), .p__i(blok_3_p__i_1), .q__i(blok_3_p__i_1_2), .y__i(out_12), .p__i_1(blok_4_p__i_1),
    .p__i_1_2(blok_4_p__i_1_2));
  blok blok_5 (
    .x__i(xi_5), .p__i(blok_4_p__i_1), .q__i(blok_4_p__i_1_2), .y__i(out_13), .p__i_1(blok_5_p__i_1),
    .p__i_1_2(blok_5_p__i_1_2));
  blok blok_6 (
    .x__i(xi_6), .p__i(blok_5_p__i_1), .q__i(blok_5_p__i_1_2), .y__i(out_14), .p__i_1(blok_6_p__i_1),
    .p__i_1_2(blok_6_p__i_1_2));
  blok blok_7 (
    .x__i(xi_7), .p__i(blok_6_p__i_1), .q__i(blok_6_p__i_1_2), .y__i(out_15), .p__i_1(blok_7_p__i_1),
    .p__i_1_2(blok_7_p__i_1_2));
  blok blok_8 (.x__i(xi_8), .p__i(blok_7_p__i_1), .q__i(blok_7_p__i_1_2), .y__i(out_16));  // open: p__i_1, p__i_1_2
endmodule

module blok (
  input  x__i,
  input  p__i,
  input  q__i,
  output y__i,
  output p__i_1,
  output p__i_1_2
);

  wire and_2_out, not_1_out, not_2_out;

  not not_1 (not_1_out, x__i);
  not not_2 (not_2_out, p__i);
  and and_1 (y__i, x__i, not_2_out);
  and and_2 (and_2_out, not_1_out, not_2_out, q__i);
  or or_1 (p__i_1, and_2_out, p__i);

  assign p__i_1_2 = x__i;
endmodule
