// Logisim project przyklad_iteracyjny_A18.circ as structural Verilog: 2 circuits, main circuit main
module main (
  input  in_1,
  input  in_2,
  input  in_3,
  input  in_4,
  input  in_5,
  input  in_6,
  input  in_7,
  input  in_8,
  output out_9
);

  wire blok_1_p0__i_1, blok_1_p1__i_1, blok_1_q__i_1, blok_2_p0__i_1, blok_2_p1__i_1, blok_2_q__i_1,
       blok_3_p0__i_1, blok_3_p1__i_1, blok_3_q__i_1, blok_4_p0__i_1, blok_4_p1__i_1, blok_4_q__i_1,
       blok_5_p0__i_1, blok_5_p1__i_1, blok_5_q__i_1, blok_6_p0__i_1, blok_6_p1__i_1, blok_6_q__i_1,
       blok_7_p0__i_1, blok_7_p1__i_1, blok_7_q__i_1;

  blok blok_1 (
    .x__i(in_1), .p1__i(1'b0), .p0__i(1'b0), .q__i(1'b0), .p1__i_1(blok_1_p1__i_1), .p0__i_1(blok_1_p0__i_1),
    .q__i_1(blok_1_q__i_1));  // open: y__i
  blok blok_2 (
    .x__i(in_3), .p1__i(blok_3_p1__i_1), .p0__i(blok_3_p0__i_1), .q__i(blok_3_q__i_1),
    .p1__i_1(blok_2_p1__i_1), .p0__i_1(blok_2_p0__i_1), .q__i_1(blok_2_q__i_1));  // open: y__i
  blok blok_3 (
    .x__i(in_2), .p1__i(blok_1_p1__i_1), .p0__i(blok_1_p0__i_1), .q__i(blok_1_q__i_1),
    .p1__i_1(blok_3_p1__i_1), .p0__i_1(blok_3_p0__i_1), .q__i_1(blok_3_q__i_1));  // open: y__i
  blok blok_4 (
    .x__i(in_4), .p1__i(blok_2_p1__i_1), .p0__i(blok_2_p0__i_1), .q__i(blok_2_q__i_1),
    .p1__i_1(blok_4_p1__i_1), .p0__i_1(blok_4_p0__i_1), .q__i_1(blok_4_q__i_1));  // open: y__i
  blok blok_5 (
    .x__i(in_5), .p1__i(blok_4_p1__i_1), .p0__i(blok_4_p0__i_1), .q__i(blok_4_q__i_1),
    .p1__i_1(blok_5_p1__i_1), .p0__i_1(blok_5_p0__i_1), .q__i_1(blok_5_q__i_1));  // open: y__i
  blok blok_6 (
    .x__i(in_6), .p1__i(blok_5_p1__i_1), .p0__i(blok_5_p0__i_1), .q__i(blok_5_q__i_1),
    .p1__i_1(blok_6_p1__i_1), .p0__i_1(blok_6_p0__i_1), .q__i_1(blok_6_q__i_1));  // open: y__i
  blok blok_7 (
    .x__i(in_7), .p1__i(blok_6_p1__i_1), .p0__i(blok_6_p0__i_1), .q__i(blok_6_q__i_1),
    .p1__i_1(blok_7_p1__i_1), .p0__i_1(blok_7_p0__i_1), .q__i_1(blok_7_q__i_1));  // open: y__i
  blok blok_8 (
    .x__i(in_8), .p1__i(blok_7_p1__i_1), .p0__i(blok_7_p0__i_1), .q__i(blok_7_q__i_1), .y__i(out_9));  // open: p1__i_1, p0__i_1, q__i_1
endmodule

module blok (
  input  x__i,
  input  p1__i,
  input  p0__i,
  input  q__i,
  output p1__i_1,
  output p0__i_1,
  output q__i_1,
  output y__i
);

  wire and_1_out, and_2_out, and_3_out, and_4_out, and_5_out, and_6_out, and_7_out, not_1_out, not_3_out,
       not_4_out;

  not not_1 (not_1_out, x__i);
  // NOT_Gate not_2 has open pins: in=p1__i, out=open
  not not_3 (not_3_out, p0__i);
  not not_4 (not_4_out, q__i);
  and and_1 (and_1_out, x__i, p0__i);
  or or_1 (p1__i_1, and_1_out, p1__i);
  and and_2 (and_2_out, p1__i, p0__i);
  and and_3 (and_3_out, not_1_out, p0__i);
  or or_2 (p0__i_1, and_2_out, and_3_out, and_4_out);
  and and_4 (and_4_out, x__i, not_3_out);
  and and_5 (and_5_out, x__i, p1__i, p0__i);
  or or_3 (q__i_1, and_5_out, q__i);
  and and_6 (and_6_out, x__i, p1__i, not_3_out, q__i);
  and and_7 (and_7_out, not_1_out, p1__i, p0__i, not_4_out);
  or or_4 (y__i, and_6_out, and_7_out);
endmodule
