// Logisim project przyklad_kpn.circ as structural Verilog: 2 circuits, main circuit main
module main (
);

  wire button_1_out, f2_1_y;
  wire [4:0] counter_1_q;

  Counter #(.width(5), .max('h1f)) counter_1 (.Q(counter_1_q), .clk(button_1_out));  // open: load, D, count, carry, clr
  Button button_1 (.out(button_1_out));
  LED led_1 (.in(f2_1_y));
  f2 f2_1 (
    .x4(counter_1_q[4]), .x3(counter_1_q[3]), .x2(counter_1_q[2]), .x1(counter_1_q[1]), .x0(counter_1_q[0]),
    .y(f2_1_y));
endmodule

module f2 (
  input  x4,
  input  x3,
  input  x2,
  input  x1,
  input  x0,
  output y
);

  wire nor_1_out, nor_2_out, nor_3_out, nor_4_out, nor_5_out, nor_6_out, not_1_out, not_2_out, not_3_out,
       not_4_out;

  not not_1 (not_1_out, x4);
  not not_2 (not_2_out, x1);
  not not_3 (not_3_out, x2);
  not not_4 (not_4_out, x0);
  nor nor_1 (nor_1_out, x2, x1, x0);
  nor nor_2 (nor_2_out, not_1_out, x3);
  nor nor_3 (nor_3_out, x4, not_3_out, not_2_out);
  nor nor_4 (nor_4_out, x3, not_3_out);
  nor nor_5 (nor_5_out, not_1_out, x1, x0);
  nor nor_6 (nor_6_out, not_1_out, not_2_out, not_4_out);
  nor nor_7 (y, nor_1_out, nor_2_out, nor_3_out, nor_4_out, nor_5_out, nor_6_out);
endmodule
