// Logisim project przyklad_laczna_B1.circ as structural Verilog: 1 circuit, main circuit main
module main (
  input  x3,
  input  x2,
  input  x1,
  input  x0,
  output y1,
  output y2,
  output y3
);

  wire nand_1_out, nand_2_out, nand_3_out, nand_4_out, nand_5_out, nand_6_out, not_1_out, not_2_out,
       not_3_out;

  not not_1 (not_1_out, x3);
  not not_2 (not_2_out, x2);
  not not_3 (not_3_out, x0);
  nand nand_1 (nand_1_out, x3, x2, x0);
  nand nand_2 (nand_2_out, not_1_out, not_2_out);
  nand nand_3 (nand_3_out, not_2_out, not_3_out);
  nand nand_4 (nand_4_out, x2, x0);
  nand nand_5 (nand_5_out, x3, x1, x0);
  nand nand_6 (nand_6_out, not_1_out, not_3_out);
  nand nand_7 (y1, nand_1_out, nand_2_out);
  nand nand_8 (y2, nand_3_out, nand_4_out);
  nand nand_9 (y3, nand_5_out, nand_4_out, nand_6_out);
endmodule
