// Logisim project przyklad_mikroprogramowanie.circ as structural Verilog: 1 circuit, main circuit main
module main (
  input  SYNC,
  input  [3:0] A,
  input  [3:0] B,
  output ACK
);

  wire _1_q, _2_q, _3_q, _4_q, _5_q, _6_q, and_1_out, and_2_out, and_3_out, and_4_out, and_5_out, and_6_out,
       and_7_out, and_8_out, Az_q, Bz_q, clock_1_out, comparator_1_eq, comparator_2_gt, multiplexer_3_out,
       not_1_out, not_2_out, not_3_out, not_4_out, not_5_out, or_1_out, or_2_out, or_3_out, or_4_out;
  wire [2:0] adder_1_out, Am_q, Bm_q, multiplexer_1_out, multiplexer_2_out, multiplexer_4_out,
       subtractor_1_out;

  Clock clock_1 (.out(clock_1_out));
  or or_1 (or_1_out, _5_q, _4_q, _3_q);
  or or_2 (or_2_out, and_8_out, and_2_out);
  Multiplexer #(.width(3), .enable("false")) multiplexer_1 (
    .in0(Bm_q), .in1(Am_q), .out(multiplexer_1_out), .sel(_5_q));
  D_Flip_Flop #(.trigger("falling")) _1 (.clk(clock_1_out), .D(or_2_out), .Q(_1_q));  // open: Qn, preset, en, reset
  Register #(.width(1)) Az (.D(A[3]), .en(and_1_out), .Q(Az_q), .clk(clock_1_out), .clr(or_2_out));
  Multiplexer #(.width(3), .enable("false")) multiplexer_2 (
    .in0(Am_q), .in1(Bm_q), .out(multiplexer_2_out), .sel(_5_q));
  Subtractor #(.width(3)) subtractor_1 (
    .a(multiplexer_1_out), .b(multiplexer_2_out), .out(subtractor_1_out));  // open: bin, bout
  not not_1 (not_1_out, _4_q);
  Multiplexer #(.enable("false")) multiplexer_3 (.in0(Bz_q), .in1(Az_q), .out(multiplexer_3_out), .sel(not_1_out));
  Register #(.width(3)) Am (.D(A[2:0]), .en(and_1_out), .Q(Am_q), .clk(clock_1_out), .clr(or_2_out));
  not not_2 (not_2_out, SYNC);
  Multiplexer #(.width(3), .enable("false")) multiplexer_4 (
    .in0(subtractor_1_out), .in1(adder_1_out), .out(multiplexer_4_out), .sel(_3_q));
  Register #(.width(1)) Wz (.D(multiplexer_3_out), .en(or_1_out), .clk(clock_1_out), .clr(and_1_out));  // open: Q
  and and_1 (and_1_out, SYNC, _1_q);
  and and_2 (and_2_out, not_2_out, _1_q);
  Register #(.width(1)) Bz (.D(B[3]), .en(and_1_out), .Q(Bz_q), .clk(clock_1_out), .clr(or_2_out));
  Register #(.width(3)) Wm (.D(multiplexer_4_out), .en(or_1_out), .clk(clock_1_out), .clr(and_1_out));  // open: Q
  Register #(.width(3)) Bm (.D(B[2:0]), .en(and_1_out), .Q(Bm_q), .clk(clock_1_out), .clr(or_2_out));
  Comparator #(.width(1), .mode("unsigned")) comparator_1 (.a(Az_q), .b(Bz_q), .eq(comparator_1_eq));  // open: gt, lt
  Comparator #(.width(3), .mode("unsigned")) comparator_2 (.a(Am_q), .b(Bm_q), .gt(comparator_2_gt));  // open: eq, lt
  Adder #(.width(3)) adder_1 (.a(Bm_q), .b(Am_q), .out(adder_1_out));  // open: cin, cout
  not not_3 (not_3_out, comparator_1_eq);
  and and_3 (and_3_out, comparator_1_eq, and_1_out);
  and and_4 (and_4_out, not_3_out, and_1_out);
  D_Flip_Flop #(.trigger("falling")) _3 (.clk(clock_1_out), .D(and_3_out), .Q(_3_q));  // open: Qn, preset, en, reset
  D_Flip_Flop #(.trigger("falling")) _2 (.clk(clock_1_out), .D(and_4_out), .Q(_2_q));  // open: Qn, preset, en, reset
  and and_5 (and_5_out, comparator_2_gt, _2_q);
  not not_4 (not_4_out, comparator_2_gt);
  and and_6 (and_6_out, not_4_out, _2_q);
  D_Flip_Flop #(.trigger("falling")) _5 (.clk(clock_1_out), .D(and_5_out), .Q(_5_q));  // open: Qn, preset, en, reset
  D_Flip_Flop #(.trigger("falling")) _4 (.clk(clock_1_out), .D(and_6_out), .Q(_4_q));  // open: Qn, preset, en, reset
  or or_3 (or_3_out, _5_q, _4_q, _3_q);
  D_Flip_Flop #(.trigger("falling")) _6 (.clk(clock_1_out), .D(or_4_out), .Q(_6_q));  // open: Qn, preset, en, reset
  or or_4 (or_4_out, and_7_out, or_3_out);
  S_R_Flip_Flop #(.trigger("falling")) s_r_ff_1 (
    .S(_6_q), .clk(clock_1_out), .R(or_2_out), .Q(ACK));  // open: Qn, preset, reset, en
  and and_7 (and_7_out, SYNC, _6_q);
  not not_5 (not_5_out, SYNC);
  and and_8 (and_8_out, not_5_out, _6_q);

  // Notes on the sheet:
  //   S1
  //   S3
  //   S0
  //   S2
  //   S4
endmodule
