// Logisim project przyklad_mikroprogramowanie_ROM.circ as structural Verilog: 1 circuit, main circuit main
module main (
  input  SYNC,
  input  [3:0] A,
  input  [3:0] B,
  output ACK
);

  wire Az_q, Bz_q, clock_1_out, comparator_1_eq, comparator_2_gt, multiplexer_3_out, multiplexer_5_out,
       not_1_out, not_2_out, not_3_out, not_4_out, not_5_out;
  wire [2:0] adder_1_out, Am_q, Bm_q, counter_1_q, multiplexer_1_out, multiplexer_2_out, multiplexer_4_out,
       rom_1_data, rom_1_data_3, subtractor_1_out;
  wire [7:3] rom_1_data_2;

  Clock clock_1 (.out(clock_1_out));
  Multiplexer #(.width(3), .enable("false")) multiplexer_1 (
    .in0(Bm_q), .in1(Am_q), .out(multiplexer_1_out), .sel(rom_1_data_2[6]));
  Register #(.width(1)) Az (.D(A[3]), .en(rom_1_data_2[3]), .Q(Az_q), .clk(clock_1_out));  // open: clr
  Multiplexer #(.width(3), .enable("false")) multiplexer_2 (
    .in0(Am_q), .in1(Bm_q), .out(multiplexer_2_out), .sel(rom_1_data_2[6]));
  Subtractor #(.width(3)) subtractor_1 (
    .a(multiplexer_1_out), .b(multiplexer_2_out), .out(subtractor_1_out));  // open: bin, bout
  not not_1 (not_1_out, rom_1_data_2[5]);
  Multiplexer #(.enable("false")) multiplexer_3 (.in0(Bz_q), .in1(Az_q), .out(multiplexer_3_out), .sel(not_1_out));
  Register #(.width(3)) Am (.D(A[2:0]), .en(rom_1_data_2[3]), .Q(Am_q), .clk(clock_1_out));  // open: clr
  Multiplexer #(.width(3), .enable("false")) multiplexer_4 (
    .in0(subtractor_1_out), .in1(adder_1_out), .out(multiplexer_4_out), .sel(rom_1_data_2[7]));
  Register #(.width(1)) Wz (
    .D(multiplexer_3_out), .en(rom_1_data_2[4]), .clk(clock_1_out), .clr(rom_1_data_2[3]));  // open: Q
  Register #(.width(1)) Bz (.D(B[3]), .en(rom_1_data_2[3]), .Q(Bz_q), .clk(clock_1_out));  // open: clr
  Register #(.width(3)) Wm (
    .D(multiplexer_4_out), .en(rom_1_data_2[4]), .clk(clock_1_out), .clr(rom_1_data_2[3]));  // open: Q
  Register #(.width(3)) Bm (.D(B[2:0]), .en(rom_1_data_2[3]), .Q(Bm_q), .clk(clock_1_out));  // open: clr
  Comparator #(.width(1), .mode("unsigned")) comparator_1 (.a(Az_q), .b(Bz_q), .eq(comparator_1_eq));  // open: gt, lt
  Comparator #(.width(3), .mode("unsigned")) comparator_2 (.a(Am_q), .b(Bm_q), .gt(comparator_2_gt));  // open: eq, lt
  Adder #(.width(3)) adder_1 (.a(Bm_q), .b(Am_q), .out(adder_1_out));  // open: cin, cout
  not not_2 (not_2_out, SYNC);
  not not_3 (not_3_out, comparator_2_gt);
  not not_4 (not_4_out, comparator_1_eq);
  Multiplexer #(.select(3), .enable("false")) multiplexer_5 (
    .in0(SYNC), .in1(not_2_out), .in2(not_4_out), .in3(not_3_out), .in4(1'b1), .in5(1'b0), .in6(1'b0),
    .in7(1'b0), .out(multiplexer_5_out), .sel(rom_1_data_3));
  not not_5 (not_5_out, multiplexer_5_out);
  Counter #(.width(3), .max('h7), .trigger("falling")) counter_1 (
    .load(not_5_out), .D(rom_1_data), .count(multiplexer_5_out), .Q(counter_1_q), .clk(clock_1_out));  // open: carry, clr
  ROM #(.addrWidth(3), .dataWidth(12)) rom_1 (
    .addr(counter_1_q), .data({rom_1_data_3, ACK, rom_1_data_2, rom_1_data}));  // open: sel

  // Notes on the sheet:
  //   S1
  //   S3
  //   S2
  //   S4
  //   contents of rom_1 (hex, n*v repeats v):
  //   0 0 0 a35
endmodule
