// Logisim project przyklad_mikroprogramowanie_ROM1.circ as structural Verilog: 1 circuit, main circuit main
module main (
  input  SYNC,
  input  [3:0] \input ,
  output ACK,
  output WYN,
  output [1:0] Y
);

  wire clock_1_out, multiplexer_1_out, nor_1_out, not_1_out, not_2_out, or_1_out;
  wire [1:0] rom_1_data_3;
  wire [2:0] counter_1_q, counter_2_q, rom_1_data;
  wire [3:0] A_q, adder_1_out, SUM_q;
  wire [10:3] rom_1_data_2;

  Clock clock_1 (.out(clock_1_out));
  Register #(.width(4)) A (.D(\input ), .en(rom_1_data_2[3]), .Q(A_q), .clk(clock_1_out), .clr(rom_1_data_2[4]));
  Adder #(.width(4)) adder_1 (.a(SUM_q), .b(\input ), .out(adder_1_out));  // open: cin, cout
  Comparator #(.width(4)) comparator_1 (.a(A_q), .b(SUM_q), .gt(Y[0]), .lt(Y[1]));  // open: eq
  Register #(.width(4)) SUM (
    .D(adder_1_out), .en(rom_1_data_2[5]), .Q(SUM_q), .clk(clock_1_out), .clr(rom_1_data_2[6]));
  or or_1 (or_1_out, rom_1_data_2[7], rom_1_data_2[8]);
  nor nor_1 (nor_1_out, counter_1_q[2], counter_1_q[1], counter_1_q[0]);
  Counter #(.width(3), .max('h4)) counter_1 (
    .load(or_1_out), .D(3'b100), .count(rom_1_data_2[8]), .Q(counter_1_q), .clk(clock_1_out));  // open: carry, clr
  not not_1 (not_1_out, SYNC);
  Multiplexer #(.select(2), .enable("false")) multiplexer_1 (
    .in0(1'b0), .in1(SYNC), .in2(not_1_out), .in3(nor_1_out), .out(multiplexer_1_out), .sel(rom_1_data_3));
  D_Flip_Flop u_ACK (
    .clk(1'b0), .D(1'b0), .Q(ACK), .preset(rom_1_data_2[9]), .reset(rom_1_data_2[10]));  // open: Qn, en
  not not_2 (not_2_out, multiplexer_1_out);
  Counter #(.width(3), .max('h7), .trigger("falling")) counter_2 (
    .load(not_2_out), .D(rom_1_data), .count(multiplexer_1_out), .Q(counter_2_q), .clk(clock_1_out));  // open: carry, clr
  ROM #(.addrWidth(3), .dataWidth(14)) rom_1 (
    .addr(counter_2_q), .data({rom_1_data_3, WYN, rom_1_data_2, rom_1_data}));  // open: sel

  // Notes on the sheet:
  //   contents of rom_1 (hex, n*v repeats v):
  //   14c8 2201 1402 3126 2a04 0 2206 3002
endmodule
