// Logisim project przyklad_mikroprogramowanie_ROM3.circ as structural Verilog: 1 circuit, main circuit main
module main (
  input  SYNC,
  input  [3:0] \input ,
  output WYN,
  output ACK,
  output [5:0] Y
);

  wire clock_1_out, multiplexer_1_out, nor_1_out, not_1_out, not_2_out, or_1_out;
  wire [2:0] rom_1_data_3;
  wire [3:0] A_q, counter_1_q, counter_2_q, rom_1_data;
  wire [5:0] adder_1_out, adder_2_out;
  wire [10:4] rom_1_data_2;

  Clock clock_1 (.out(clock_1_out));
  Register #(.width(4)) A (.D({1'b0, \input [2:0]}), .en(rom_1_data_2[4]), .Q(A_q), .clk(clock_1_out));  // open: clr
  Adder #(.width(6)) adder_1 (.a({A_q, 2'b00}), .b({2'b00, A_q}), .out(adder_1_out));  // open: cin, cout
  Adder #(.width(6)) adder_2 (.a(adder_1_out), .b(Y), .out(adder_2_out));  // open: cin, cout
  Register #(.width(6)) u_Y (.D(adder_2_out), .en(rom_1_data_2[7]), .Q(Y), .clk(clock_1_out), .clr(rom_1_data_2[8]));
  or or_1 (or_1_out, rom_1_data_2[5], rom_1_data_2[6]);
  nor nor_1 (nor_1_out, counter_1_q[3], counter_1_q[2], counter_1_q[1], counter_1_q[0]);
  Counter #(.width(4), .max('hf)) counter_1 (
    .load(or_1_out), .D({1'b0, \input [2:0]}), .count(rom_1_data_2[6]), .Q(counter_1_q), .clk(clock_1_out));  // open: carry, clr
  not not_1 (not_1_out, SYNC);
  Multiplexer #(.select(3), .enable("false")) multiplexer_1 (
    .in0(SYNC), .in1(not_1_out), .in2(1'b1), .in3(1'b0), .in4(nor_1_out), .in5(1'b0), .in6(1'b0), .in7(1'b0),
    .out(multiplexer_1_out), .sel(rom_1_data_3));
  D_Flip_Flop u_ACK (
    .clk(1'b0), .D(1'b0), .Q(ACK), .preset(rom_1_data_2[9]), .reset(rom_1_data_2[10]));  // open: Qn, en
  not not_2 (not_2_out, multiplexer_1_out);
  Counter #(.width(4), .max('hf), .trigger("falling")) counter_2 (
    .load(not_2_out), .D(rom_1_data), .count(multiplexer_1_out), .Q(counter_2_q), .clk(clock_1_out));  // open: carry, clr
  ROM #(.addrWidth(4), .dataWidth(15)) rom_1 (
    .addr(counter_2_q), .data({rom_1_data_3, WYN, rom_1_data_2, rom_1_data}));  // open: sel

  // Notes on the sheet:
  //   contents of rom_1 (hex, n*v repeats v):
  //   500 2010 1202 403 2020 4008 1a06 3000 30c5
endmodule
