// Logisim project przyklad_mux_C6.circ as structural Verilog: 2 circuits, main circuit main
module main (
  input  x3,
  input  x2,
  input  x1,
  input  x0,
  output y
);

  wire mux_1_y, not_1_out;

  not not_1 (not_1_out, x0);
  mux mux_1 (.x3(1'b1), .x2(1'b1), .x1(1'b1), .x0(1'b0), .s1(not_1_out), .s0(x2), .y(mux_1_y));
  mux mux_2 (.x3(1'b0), .x2(mux_1_y), .x1(1'b1), .x0(x2), .s1(x3), .s0(x1), .y(y));
endmodule

module mux (
  input  x3,
  input  x2,
  input  x1,
  input  x0,
  input  s1,
  input  s0,
  output y
);

  wire not_1_out, not_2_out, x0_out, x1_out, x2_out, x3_out;

  not not_1 (not_1_out, s0);
  not not_2 (not_2_out, s1);
  and u_x3 (x3_out, s1, s0, x3);
  and u_x2 (x2_out, s1, not_1_out, x2);
  and u_x1 (x1_out, not_2_out, s0, x1);
  and u_x0 (x0_out, not_2_out, not_1_out, x0);
  or or_1 (y, x3_out, x2_out, x1_out, x0_out);
endmodule
