// Logisim project przyklad_nieRnieS.circ as structural Verilog: 7 circuits, main circuit main
module main (
  input  a,
  input  b,
  output y
);

  wire not_1_out, not_2_out, not_3_out, not_4_out, not_5_out, not_6_out, Q0_q, Q1_q, Q2_q, r0_1_y, r1_1_y,
       r2_1_y, s0_1_y, s1_1_y, s2_1_y;

  S2 s2_1 (.Q2(Q2_q), .Q1(Q1_q), .Q0(Q0_q), .a(a), .b(b), .y(s2_1_y));
  R2 r2_1 (.Q2(Q2_q), .Q1(Q1_q), .Q0(Q0_q), .a(a), .b(b), .y(r2_1_y));
  S1 s1_1 (.Q2(Q2_q), .Q1(Q1_q), .Q0(Q0_q), .a(a), .b(b), .y(s1_1_y));
  R1 r1_1 (.Q2(Q2_q), .Q1(Q1_q), .Q0(Q0_q), .a(a), .b(b), .y(r1_1_y));
  S0 s0_1 (.Q2(Q2_q), .Q1(Q1_q), .Q0(Q0_q), .a(a), .b(b), .y(s0_1_y));
  R0 r0_1 (.Q2(Q2_q), .Q1(Q1_q), .Q0(Q0_q), .a(a), .b(b), .y(r0_1_y));
  not not_1 (not_1_out, s2_1_y);
  not not_2 (not_2_out, r2_1_y);
  not not_3 (not_3_out, s1_1_y);
  not not_4 (not_4_out, r1_1_y);
  not not_5 (not_5_out, s0_1_y);
  not not_6 (not_6_out, r0_1_y);
  D_Flip_Flop Q2 (.clk(1'b0), .D(1'b0), .Q(Q2_q), .preset(not_1_out), .reset(not_2_out));  // open: Qn, en
  D_Flip_Flop Q1 (.clk(1'b0), .D(1'b0), .Q(Q1_q), .preset(not_3_out), .reset(not_4_out));  // open: Qn, en
  D_Flip_Flop Q0 (.clk(1'b0), .D(1'b0), .Q(Q0_q), .preset(not_5_out), .reset(not_6_out));  // open: Qn, en
endmodule

module R0 (
  input  Q2,
  input  Q1,
  input  Q0,
  input  a,
  input  b,
  output y
);

  wire and_1_out, and_2_out, and_3_out, not_1_out, not_2_out, not_3_out, not_4_out, not_5_out, not_6_out;

  not not_1 (not_1_out, Q2);
  not not_2 (not_2_out, b);
  not not_3 (not_3_out, Q1);
  not not_4 (not_4_out, a);
  not not_5 (not_5_out, a);
  not not_6 (not_6_out, b);
  and and_1 (and_1_out, not_1_out, not_2_out);
  and and_2 (and_2_out, not_3_out, not_4_out);
  and and_3 (and_3_out, not_5_out, not_6_out);
  or or_1 (y, and_1_out, and_2_out, and_3_out);
endmodule

module R1 (
  input  Q2,
  input  Q1,
  input  Q0,
  input  a,
  input  b,
  output y
);

  wire and_1_out, and_2_out, and_3_out, not_1_out, not_2_out, not_3_out, not_4_out;

  not not_1 (not_1_out, Q0);
  not not_2 (not_2_out, a);
  not not_3 (not_3_out, Q0);
  not not_4 (not_4_out, a);
  and and_1 (and_1_out, not_1_out, not_2_out);
  and and_2 (and_2_out, not_3_out, b);
  and and_3 (and_3_out, not_4_out, b);
  or or_1 (y, and_1_out, and_2_out, and_3_out);
endmodule

module R2 (
  input  Q2,
  input  Q1,
  input  Q0,
  input  a,
  input  b,
  output y
);

  wire and_1_out, and_2_out, and_3_out, and_4_out, not_1_out, not_2_out, not_3_out, not_4_out;

  not not_1 (not_1_out, Q0);
  not not_2 (not_2_out, Q1);
  not not_3 (not_3_out, a);
  not not_4 (not_4_out, Q0);
  and and_1 (and_1_out, not_1_out, b);
  and and_2 (and_2_out, not_2_out, a);
  and and_3 (and_3_out, Q0, not_3_out);
  and and_4 (and_4_out, Q1, not_4_out);
  or or_1 (y, and_1_out, and_2_out, and_3_out, and_4_out);
endmodule

module S2 (
  input  Q2,
  input  Q1,
  input  Q0,
  input  a,
  input  b,
  output y
);

  wire and_1_out, not_1_out, not_2_out;

  not not_1 (not_1_out, Q0);
  not not_2 (not_2_out, b);
  and and_1 (and_1_out, not_1_out, not_2_out);
  or or_1 (y, and_1_out, a, Q2);
endmodule

module S1 (
  input  Q2,
  input  Q1,
  input  Q0,
  input  a,
  input  b,
  output y
);

  wire and_1_out, not_1_out, not_2_out, not_3_out, not_4_out;

  not not_1 (not_1_out, Q0);
  not not_2 (not_2_out, a);
  not not_3 (not_3_out, Q2);
  and and_1 (and_1_out, not_1_out, not_2_out);
  not not_4 (not_4_out, b);
  or or_1 (y, not_3_out, and_1_out, not_4_out);
endmodule

module S0 (
  input  Q2,
  input  Q1,
  input  Q0,
  input  a,
  input  b,
  output y
);

  wire and_1_out, and_2_out, not_1_out, not_2_out;

  not not_1 (not_1_out, Q1);
  not not_2 (not_2_out, a);
  and and_1 (and_1_out, not_1_out, not_2_out);
  and and_2 (and_2_out, Q2, a);
  or or_1 (y, and_1_out, b, Q0, and_2_out);
endmodule
